// Logisim project Aula_05-11.circ as structural Verilog: 16 circuits, main circuit main
module main (
);

  wire clock_1_out, not_1_out, not_2_out, Ovflw_q, Reset_out, ula_1_overflow, ula_1_zero,
       unidade_de_controle_1_clk_ac, unidade_de_controle_1_clk_ir, unidade_de_controle_1_clk_pc,
       unidade_de_controle_1_clk_ram, unidade_de_controle_1_d, unidade_de_controle_1_e,
       unidade_de_controle_1_load, unidade_de_controle_1_r_1_w_0, unidade_de_controle_1_rst_pc, Zero_q;
  wire [2:0] unidade_de_controle_1_opcode;
  wire [3:0] ac_1_s, mux_1_out_4, PC_q, ram_1_data, ula_1_out_6, unidade_de_controle_1_dados,
       unidade_de_controle_1_operando;
  wire [7:0] ir_1_s, rom_1_data;

  not not_1 (not_1_out, unidade_de_controle_1_load);
  Clock clock_1 (.out(clock_1_out));
  Button Reset (.out(Reset_out));
  Counter #(.width(4), .max('hf)) PC (
    .load(unidade_de_controle_1_load), .D(unidade_de_controle_1_dados), .count(not_1_out), .Q(PC_q),
    .clk(unidade_de_controle_1_clk_pc), .clr(unidade_de_controle_1_rst_pc));  // open: carry
  Unidade_de_Controle unidade_de_controle_1 (
    .Clock(clock_1_out), .Reset(Reset_out), .Rst_PC(unidade_de_controle_1_rst_pc), .\Instrução (ir_1_s),
    .Operando(unidade_de_controle_1_operando), .D(unidade_de_controle_1_d),
    .Opcode(unidade_de_controle_1_opcode), .clk_IR(unidade_de_controle_1_clk_ir),
    .clk_PC(unidade_de_controle_1_clk_pc), .clk_AC(unidade_de_controle_1_clk_ac),
    .clk_RAM(unidade_de_controle_1_clk_ram), .Ovflw(Ovflw_q), .Zero(Zero_q),
    .Load(unidade_de_controle_1_load), .R_1_W_0(unidade_de_controle_1_r_1_w_0), .E(unidade_de_controle_1_e),
    .Dados(unidade_de_controle_1_dados));
  ROM #(.addrWidth(4)) rom_1 (.addr(PC_q), .data(rom_1_data));  // open: sel
  IR ir_1 (.Clock(unidade_de_controle_1_clk_ir), .A(rom_1_data), .S(ir_1_s));
  // Probe on ac_1_s
  MUX mux_1 (.in_3(unidade_de_controle_1_e), .A(unidade_de_controle_1_operando), .B(ram_1_data), .out_4(mux_1_out_4));
  ULA ula_1 (
    .D(unidade_de_controle_1_d), .A(ac_1_s), .B(mux_1_out_4), .in_4(unidade_de_controle_1_opcode),
    .Overflow(ula_1_overflow), .Zero(ula_1_zero), .out_6(ula_1_out_6));
  AC ac_1 (.Clock(unidade_de_controle_1_clk_ac), .S(ac_1_s), .A(ula_1_out_6));
  D_Flip_Flop Ovflw (
    .clk(unidade_de_controle_1_clk_ac), .D(ula_1_overflow), .Q(Ovflw_q));  // open: Qn, preset, en, reset
  D_Flip_Flop Zero (.clk(unidade_de_controle_1_clk_ac), .D(ula_1_zero), .Q(Zero_q));  // open: Qn, preset, en, reset
  RAM #(.addrWidth(4), .dataWidth(4)) ram_1 (
    .addr(unidade_de_controle_1_operando), .data(ram_1_data), .clk(unidade_de_controle_1_clk_ram),
    .ld(unidade_de_controle_1_r_1_w_0));  // open: sel, clr
  not not_2 (not_2_out, unidade_de_controle_1_r_1_w_0);
  Buffer_3_State buffer_3_state_1 (.A(ac_1_s), .in_2(not_2_out), .S(ram_1_data));

  // Notes on the sheet:
  //   contents of rom_1 (hex, n*v repeats v):
  //   0 f0 1 f1 10 31 d0 f2 11 f0 12 f1 e4
endmodule

module Decodificador_3x8 (
  input  [2:0] c,
  output s0,
  output s1,
  output s2,
  output s3,
  output s4,
  output s5,
  output s6,
  output s7
);

  wire not_1_out, not_2_out, not_3_out, not_4_out, not_5_out, not_6_out, not_7_out, not_8_out, not_9_out,
       not_10_out, not_11_out, not_12_out;

  not not_1 (not_1_out, c[2]);
  not not_2 (not_2_out, c[1]);
  not not_3 (not_3_out, c[0]);
  not not_4 (not_4_out, c[2]);
  not not_5 (not_5_out, c[1]);
  not not_6 (not_6_out, c[2]);
  not not_7 (not_7_out, c[0]);
  not not_8 (not_8_out, c[2]);
  not not_9 (not_9_out, c[1]);
  not not_10 (not_10_out, c[0]);
  not not_11 (not_11_out, c[1]);
  not not_12 (not_12_out, c[0]);
  and and_1 (s7, c[2], c[1], c[0]);
  and and_2 (s0, not_1_out, not_2_out, not_3_out);
  and and_3 (s1, not_4_out, not_5_out, c[0]);
  and and_4 (s2, not_6_out, c[1], not_7_out);
  and and_5 (s3, not_8_out, c[1], c[0]);
  and and_6 (s4, c[2], not_9_out, not_10_out);
  and and_7 (s5, c[2], not_11_out, c[0]);
  and and_8 (s6, c[2], c[1], not_12_out);
endmodule

module Buffer_3_State (
  input  [3:0] A,
  input  in_2,
  output [3:0] S
);

  assign S[3] = in_2 ? A[3] : 1'bz;  // Controlled_Buffer controlled_buffer_1
  assign S[2] = in_2 ? A[2] : 1'bz;  // Controlled_Buffer controlled_buffer_2
  assign S[0] = in_2 ? A[0] : 1'bz;  // Controlled_Buffer controlled_buffer_3
  assign S[1] = in_2 ? A[1] : 1'bz;  // Controlled_Buffer controlled_buffer_4
endmodule

module Add_1 (
  input  a,
  input  b,
  input  Vem_1,
  output Soma,
  output Vai_1
);

  wire and_1_out, and_2_out, or_1_out, xor_1_out;

  xor xor_1 (xor_1_out, b, a);
  or or_1 (or_1_out, Vem_1, b);
  and and_1 (and_1_out, Vem_1, b);
  xor xor_2 (Soma, Vem_1, xor_1_out);
  and and_2 (and_2_out, or_1_out, a);
  or or_2 (Vai_1, and_2_out, and_1_out);
endmodule

module Rot_Esq (
  input  [3:0] ABCD,
  input  [1:0] XY,
  output [3:0] abcd_2
);

  wire and_1_out, and_2_out, and_3_out, and_4_out, and_5_out, and_6_out, and_7_out, and_8_out, and_9_out;

  and and_1 (and_1_out, ~XY[1], ~XY[0], ABCD[3]);  // AND_Gate
  and and_2 (and_2_out, ~XY[1], XY[0], ABCD[2]);  // AND_Gate
  and and_3 (and_3_out, XY[1], ~XY[0], ABCD[1]);  // AND_Gate
  and and_4 (and_4_out, XY[1], XY[0], ABCD[0]);
  and and_5 (and_5_out, ~XY[1], ~XY[0], ABCD[2]);  // AND_Gate
  and and_6 (and_6_out, ~XY[1], XY[0], ABCD[1]);  // AND_Gate
  and and_7 (and_7_out, XY[1], ~XY[0], ABCD[0]);  // AND_Gate
  and and_8 (and_8_out, ~XY[1], ~XY[0], ABCD[1]);  // AND_Gate
  and and_9 (and_9_out, ~XY[1], XY[0], ABCD[0]);  // AND_Gate
  and and_10 (abcd_2[0], ~XY[1], ~XY[0], ABCD[0]);  // AND_Gate
  or or_1 (abcd_2[3], and_1_out, and_2_out, and_3_out, and_4_out);
  or or_2 (abcd_2[2], and_5_out, and_6_out, and_7_out);
  or or_3 (abcd_2[1], and_8_out, and_9_out);
endmodule

module Rot_Dir (
  input  [3:0] ABCD,
  input  [1:0] XY,
  output [3:0] abcd_2
);

  wire and_1_out, and_2_out, and_3_out, and_4_out, and_5_out, and_6_out, and_7_out, and_8_out, and_9_out;

  and and_1 (and_1_out, ~XY[1], ~XY[0], ABCD[0]);  // AND_Gate
  and and_2 (and_2_out, ~XY[1], XY[0], ABCD[1]);  // AND_Gate
  and and_3 (and_3_out, XY[1], ~XY[0], ABCD[2]);  // AND_Gate
  and and_4 (and_4_out, XY[1], XY[0], ABCD[3]);
  and and_5 (and_5_out, ~XY[1], ~XY[0], ABCD[1]);  // AND_Gate
  and and_6 (and_6_out, ~XY[1], XY[0], ABCD[2]);  // AND_Gate
  and and_7 (and_7_out, XY[1], ~XY[0], ABCD[3]);  // AND_Gate
  and and_8 (and_8_out, ~XY[1], ~XY[0], ABCD[2]);  // AND_Gate
  and and_9 (and_9_out, ~XY[1], XY[0], ABCD[3]);  // AND_Gate
  and and_10 (abcd_2[3], ~XY[1], ~XY[0], ABCD[3]);  // AND_Gate
  or or_1 (abcd_2[0], and_1_out, and_2_out, and_3_out, and_4_out);
  or or_2 (abcd_2[1], and_5_out, and_6_out, and_7_out);
  or or_3 (abcd_2[2], and_8_out, and_9_out);
endmodule

module Add_4 (
  input  [3:0] A,
  input  [3:0] B,
  output Overflow,
  output [3:0] Soma
);

  wire add_1_2_vai_1, add_1_3_vai_1, add_1_4_vai_1;

  // Probe on A
  Add_1 add_1_1 (.Soma(Soma[3]), .Vai_1(Overflow), .a(A[3]), .b(B[3]), .Vem_1(add_1_2_vai_1));
  Add_1 add_1_2 (.Soma(Soma[2]), .Vai_1(add_1_2_vai_1), .a(A[2]), .b(B[2]), .Vem_1(add_1_3_vai_1));
  Add_1 add_1_3 (.Soma(Soma[1]), .Vai_1(add_1_3_vai_1), .a(A[1]), .b(B[1]), .Vem_1(add_1_4_vai_1));
  // Probe on Soma
  // Probe on B
  Add_1 add_1_4 (.Soma(Soma[0]), .Vai_1(add_1_4_vai_1), .a(A[0]), .b(B[0]), .Vem_1(1'b0));
endmodule

module Sub_1 (
  input  a,
  input  b,
  input  Vem_1,
  output S,
  output Vai_1
);

  wire and_1_out, and_2_out, or_1_out, xor_1_out;

  xor xor_1 (xor_1_out, b, a);
  or or_1 (or_1_out, Vem_1, b);
  and and_1 (and_1_out, or_1_out, ~a);  // AND_Gate
  and and_2 (and_2_out, b, Vem_1);
  xor xor_2 (S, Vem_1, xor_1_out);
  or or_2 (Vai_1, and_1_out, and_2_out);
endmodule

module Sub_4 (
  input  [3:0] B,
  input  [3:0] A,
  output Vai_1,
  output [3:0] S
);

  wire sub_1_2_vai_1, sub_1_3_vai_1, sub_1_4_vai_1;

  // Probe on A
  Sub_1 sub_1_1 (.S(S[3]), .Vai_1(Vai_1), .a(A[3]), .b(B[3]), .Vem_1(sub_1_2_vai_1));
  Sub_1 sub_1_2 (.S(S[2]), .Vai_1(sub_1_2_vai_1), .a(A[2]), .b(B[2]), .Vem_1(sub_1_3_vai_1));
  Sub_1 sub_1_3 (.S(S[1]), .Vai_1(sub_1_3_vai_1), .a(A[1]), .b(B[1]), .Vem_1(sub_1_4_vai_1));
  // Probe on S
  Sub_1 sub_1_4 (.S(S[0]), .Vai_1(sub_1_4_vai_1), .a(A[0]), .b(B[0]), .Vem_1(1'b0));
  // Probe on B
endmodule

module Or_4bits (
  input  [3:0] B,
  input  [3:0] A,
  output [3:0] S
);

  or or_1 (S[3], A[3], B[3]);
  or or_2 (S[2], A[2], B[2]);
  or or_3 (S[1], A[1], B[1]);
  or or_4 (S[0], A[0], B[0]);
endmodule

module Not_4bits (
  input  [3:0] B,
  output [3:0] S
);

  not not_1 (S[2], B[2]);
  not not_2 (S[1], B[1]);
  not not_3 (S[3], B[3]);
  not not_4 (S[0], B[0]);
endmodule

module ULA (
  input  D,
  input  [3:0] A,
  input  [3:0] B,
  input  [2:0] in_4,
  output Overflow,
  output [3:0] out_6,
  output Zero
);

  wire add_4_1_overflow, and_1_out, and_2_out, decodificador_3x8_1_s0, decodificador_3x8_1_s1,
       decodificador_3x8_1_s2, decodificador_3x8_1_s3, decodificador_3x8_1_s4, decodificador_3x8_1_s5,
       decodificador_3x8_1_s6, decodificador_3x8_1_s7, not_1_out, sub_4_1_vai_1;
  wire [3:0] add_4_1_soma, buffer_3_state_7_s, not_4bits_1_s, or_4bits_1_s, rot_dir_1_abcd_2,
       rot_esq_1_abcd_2, sub_4_1_s;

  and and_1 (and_1_out, add_4_1_overflow, decodificador_3x8_1_s1);
  or or_1 (Overflow, and_1_out, and_2_out);
  and and_2 (and_2_out, decodificador_3x8_1_s2, sub_4_1_vai_1);
  Decodificador_3x8 decodificador_3x8_1 (
    .s0(decodificador_3x8_1_s0), .s1(decodificador_3x8_1_s1), .s2(decodificador_3x8_1_s2),
    .s3(decodificador_3x8_1_s3), .s4(decodificador_3x8_1_s4), .s5(decodificador_3x8_1_s5),
    .s6(decodificador_3x8_1_s6), .s7(decodificador_3x8_1_s7), .c(in_4));
  Buffer_3_State buffer_3_state_1 (.A(B), .in_2(decodificador_3x8_1_s0), .S(out_6));
  Add_4 add_4_1 (.B(B), .A(A), .Soma(add_4_1_soma), .Overflow(add_4_1_overflow));
  Buffer_3_State buffer_3_state_2 (.A(add_4_1_soma), .in_2(decodificador_3x8_1_s1), .S(out_6));
  Sub_4 sub_4_1 (.A(A), .B(B), .S(sub_4_1_s), .Vai_1(sub_4_1_vai_1));
  Buffer_3_State buffer_3_state_3 (.A(or_4bits_1_s), .in_2(decodificador_3x8_1_s3), .S(out_6));
  Buffer_3_State buffer_3_state_4 (.A(sub_4_1_s), .in_2(decodificador_3x8_1_s2), .S(out_6));
  Or_4bits or_4bits_1 (.A(A), .B(B), .S(or_4bits_1_s));
  Not_4bits not_4bits_1 (.B(B), .S(not_4bits_1_s));
  Buffer_3_State buffer_3_state_5 (.A(not_4bits_1_s), .in_2(decodificador_3x8_1_s4), .S(out_6));
  nor nor_1 (Zero, out_6[0], out_6[1], out_6[2], out_6[3], decodificador_3x8_1_s6, decodificador_3x8_1_s7);
  Buffer_3_State buffer_3_state_6 (.A(buffer_3_state_7_s), .in_2(decodificador_3x8_1_s5), .S(out_6));
  Rot_Esq rot_esq_1 (.abcd_2(rot_esq_1_abcd_2), .ABCD(A), .XY(B[1:0]));
  not not_1 (not_1_out, D);
  Rot_Dir rot_dir_1 (.abcd_2(rot_dir_1_abcd_2), .ABCD(A), .XY(B[1:0]));
  Buffer_3_State buffer_3_state_7 (.A(rot_esq_1_abcd_2), .in_2(not_1_out), .S(buffer_3_state_7_s));
  Buffer_3_State buffer_3_state_8 (.A(rot_dir_1_abcd_2), .in_2(D), .S(buffer_3_state_7_s));
endmodule

module AC (
  input  Clock,
  input  [3:0] A,
  output [3:0] S
);

  D_Flip_Flop d_ff_1 (.clk(Clock), .D(A[3]), .Q(S[3]));  // open: Qn, preset, en, reset
  D_Flip_Flop d_ff_2 (.clk(Clock), .D(A[2]), .Q(S[2]));  // open: Qn, preset, en, reset
  D_Flip_Flop d_ff_3 (.clk(Clock), .D(A[1]), .Q(S[1]));  // open: Qn, preset, en, reset
  D_Flip_Flop d_ff_4 (.clk(Clock), .D(A[0]), .Q(S[0]));  // open: Qn, preset, en, reset
endmodule

module MUX (
  input  [3:0] A,
  input  [3:0] B,
  input  in_3,
  output [3:0] out_4
);

  wire not_1_out;

  not not_1 (not_1_out, in_3);
  Buffer_3_State buffer_3_state_1 (.A(B), .in_2(in_3), .S(out_4));
  Buffer_3_State buffer_3_state_2 (.A(A), .in_2(not_1_out), .S(out_4));
endmodule

module IR (
  input  Clock,
  input  [7:0] A,
  output [7:0] S
);

  D_Flip_Flop d_ff_1 (.clk(Clock), .D(A[7]), .Q(S[7]));  // open: Qn, preset, en, reset
  D_Flip_Flop d_ff_2 (.clk(Clock), .D(A[6]), .Q(S[6]));  // open: Qn, preset, en, reset
  D_Flip_Flop d_ff_3 (.clk(Clock), .D(A[5]), .Q(S[5]));  // open: Qn, preset, en, reset
  D_Flip_Flop d_ff_4 (.clk(Clock), .D(A[4]), .Q(S[4]));  // open: Qn, preset, en, reset
  D_Flip_Flop d_ff_5 (.clk(Clock), .D(A[3]), .Q(S[3]));  // open: Qn, preset, en, reset
  D_Flip_Flop d_ff_6 (.clk(Clock), .D(A[2]), .Q(S[2]));  // open: Qn, preset, en, reset
  D_Flip_Flop d_ff_7 (.clk(Clock), .D(A[1]), .Q(S[1]));  // open: Qn, preset, en, reset
  D_Flip_Flop d_ff_8 (.clk(Clock), .D(A[0]), .Q(S[0]));  // open: Qn, preset, en, reset
endmodule

module Unidade_de_Controle (
  input  [7:0] \Instrução ,
  input  Clock,
  input  Reset,
  input  Ovflw,
  input  Zero,
  output [3:0] Dados,
  output [3:0] Operando,
  output clk_IR,
  output clk_PC,
  output clk_AC,
  output clk_RAM,
  output D,
  output Rst_PC,
  output [2:0] Opcode,
  output R_1_W_0,
  output E,
  output Load
);

  wire and_5_out, GoTo_out, JZ_2_out, JZ_out, Storage_out;
  wire [1:0] counter_1_q;

  Counter #(.width(2), .max('h3)) counter_1 (.Q(counter_1_q), .clk(Clock), .clr(Reset));  // open: load, D, count, carry
  and Storage (Storage_out, \Instrução [7], \Instrução [6], \Instrução [5], \Instrução [4], clk_AC);
  not not_1 (R_1_W_0, Storage_out);
  and and_1 (clk_PC, ~counter_1_q[1], counter_1_q[0]);  // AND_Gate
  and and_2 (clk_IR, ~counter_1_q[1], ~counter_1_q[0]);  // AND_Gate
  and JZ (JZ_out, \Instrução [7], \Instrução [6], ~\Instrução [5], \Instrução [4], clk_PC, Ovflw);  // AND_Gate
  and and_3 (clk_AC, counter_1_q[1], ~counter_1_q[0]);  // AND_Gate
  and and_4 (clk_RAM, counter_1_q[1], counter_1_q[0]);
  and JZ_2 (JZ_2_out, \Instrução [7], \Instrução [6], ~\Instrução [5], ~\Instrução [4], clk_PC, Zero);  // AND_Gate
  or or_1 (Load, JZ_out, JZ_2_out, GoTo_out);
  and GoTo (GoTo_out, \Instrução [7], \Instrução [6], \Instrução [5], ~\Instrução [4], clk_PC);  // AND_Gate
  and and_5 (and_5_out, \Instrução [7], ~\Instrução [6], \Instrução [5]);  // AND_Gate
  and and_6 (E, ~and_5_out, \Instrução [5]);  // AND_Gate

  assign D = \Instrução [4];
  assign Dados = \Instrução [3:0];
  assign Opcode = \Instrução [7:5];
  assign Operando = \Instrução [3:0];
  assign Rst_PC = Reset;
endmodule
