// Logisim project Aula_27-08.circ as structural Verilog
module Decodificador_3x8 (
  input  [2:0] c,
  output s0,
  output s1,
  output s2,
  output s3,
  output s4,
  output s5,
  output s6,
  output s7
);

  wire not_1_out, not_2_out, not_3_out, not_4_out, not_5_out, not_6_out, not_7_out, not_8_out, not_9_out,
       not_10_out, not_11_out, not_12_out;

  not not_1 (not_1_out, c[2]);
  not not_2 (not_2_out, c[1]);
  not not_3 (not_3_out, c[0]);
  not not_4 (not_4_out, c[2]);
  not not_5 (not_5_out, c[1]);
  not not_6 (not_6_out, c[2]);
  not not_7 (not_7_out, c[0]);
  not not_8 (not_8_out, c[2]);
  not not_9 (not_9_out, c[1]);
  not not_10 (not_10_out, c[0]);
  not not_11 (not_11_out, c[1]);
  not not_12 (not_12_out, c[0]);
  and and_1 (s7, c[2], c[1], c[0]);
  and and_2 (s0, not_1_out, not_2_out, not_3_out);
  and and_3 (s1, not_4_out, not_5_out, c[0]);
  and and_4 (s2, not_6_out, c[1], not_7_out);
  and and_5 (s3, not_8_out, c[1], c[0]);
  and and_6 (s4, c[2], not_9_out, not_10_out);
  and and_7 (s5, c[2], not_11_out, c[0]);
  and and_8 (s6, c[2], c[1], not_12_out);
endmodule

module Buffer_3_State (
  input  [3:0] A,
  input  in_2,
  output [3:0] S
);

  assign S[2] = in_2 ? A[2] : 1'bz;  // Controlled_Buffer controlled_buffer_1
  assign S[3] = in_2 ? A[3] : 1'bz;  // Controlled_Buffer controlled_buffer_2
  assign S[0] = in_2 ? A[0] : 1'bz;  // Controlled_Buffer controlled_buffer_3
  assign S[1] = in_2 ? A[1] : 1'bz;  // Controlled_Buffer controlled_buffer_4
endmodule

module Add_1 (
  input  a,
  input  b,
  input  Vem_1,
  output Soma,
  output Vai_1
);

  wire and_1_out, and_2_out, or_1_out, xor_1_out;

  xor xor_1 (xor_1_out, b, a);
  or or_1 (or_1_out, Vem_1, b);
  and and_1 (and_1_out, Vem_1, b);
  xor xor_2 (Soma, Vem_1, xor_1_out);
  and and_2 (and_2_out, or_1_out, a);
  or or_2 (Vai_1, and_2_out, and_1_out);
endmodule
