// Logisim project add_1.circ as structural Verilog: 2 circuits, main circuit main
module main (
  input  in_1,
  input  in_2,
  input  in_3,
  output out_4,
  output out_5
);

  Circuito_1 circuito_1_1 (.out_4(out_5), .out_5(out_4), .in_1(in_1), .in_2(in_2), .in_3(in_3));
endmodule

module Circuito_1 (
  input  in_1,
  input  in_2,
  input  in_3,
  output out_4,
  output out_5
);

  wire and_1_out, and_2_out, or_1_out, xor_1_out;

  xor xor_1 (xor_1_out, in_2, in_1);
  or or_1 (or_1_out, in_3, in_2);
  and and_1 (and_1_out, in_2, in_3);
  and and_2 (and_2_out, or_1_out, in_1);
  xor xor_2 (out_4, in_3, xor_1_out);
  or or_2 (out_5, and_2_out, and_1_out);

  // Notes on the sheet:
  //   texto
endmodule
