// Logisim project add_4.circ as structural Verilog: 2 circuits, main circuit main
module main (
  input  [3:0] in_1,
  input  [3:0] in_2,
  output out_3,
  output [3:0] out_4
);

  wire circuito_1_2_out_5, circuito_1_3_out_5, circuito_1_4_out_5;

  // Probe on in_2
  Circuito_1 circuito_1_1 (.out_4(out_4[3]), .out_5(out_3), .in_1(in_2[3]), .in_2(in_1[3]), .in_3(circuito_1_2_out_5));
  Circuito_1 circuito_1_2 (
    .out_4(out_4[2]), .out_5(circuito_1_2_out_5), .in_1(in_2[2]), .in_2(in_1[2]), .in_3(circuito_1_3_out_5));
  // Probe on out_4
  Circuito_1 circuito_1_3 (
    .out_4(out_4[1]), .out_5(circuito_1_3_out_5), .in_1(in_2[1]), .in_2(in_1[1]), .in_3(circuito_1_4_out_5));
  Circuito_1 circuito_1_4 (.out_4(out_4[0]), .out_5(circuito_1_4_out_5), .in_1(in_2[0]), .in_2(in_1[0]), .in_3(1'b0));
  // Probe on in_1
endmodule

module Circuito_1 (
  input  in_1,
  input  in_2,
  input  in_3,
  output out_4,
  output out_5
);

  wire and_1_out, and_2_out, or_1_out, xor_1_out;

  xor xor_1 (xor_1_out, in_2, in_1);
  or or_1 (or_1_out, in_3, in_2);
  and and_1 (and_1_out, in_2, in_3);
  and and_2 (and_2_out, or_1_out, in_1);
  xor xor_2 (out_4, in_3, xor_1_out);
  or or_2 (out_5, and_2_out, and_1_out);
endmodule
