// Logisim project sub-1-e-sub-4.circ as structural Verilog: 3 circuits, main circuit main
module main (
  input  in_1,
  input  [3:0] in_2,
  input  [3:0] in_3,
  output [3:0] out_4
);

  wire sub_1_2_out_5, sub_1_3_out_5, sub_1_4_out_5;

  // Probe on in_2
  SUB_1 sub_1_1 (.out_4(out_4[3]), .in_1(in_2[3]), .in_2(in_3[3]), .in_3(sub_1_2_out_5));  // open: out_5
  SUB_1 sub_1_2 (.out_4(out_4[2]), .out_5(sub_1_2_out_5), .in_1(in_2[2]), .in_2(in_3[2]), .in_3(sub_1_3_out_5));
  // Probe on out_4
  SUB_1 sub_1_3 (.out_4(out_4[1]), .out_5(sub_1_3_out_5), .in_1(in_2[1]), .in_2(in_3[1]), .in_3(sub_1_4_out_5));
  SUB_1 sub_1_4 (.out_4(out_4[0]), .out_5(sub_1_4_out_5), .in_1(in_2[0]), .in_2(in_3[0]), .in_3(in_1));
  // Probe on in_3
endmodule

module exe_1 (
  input  A,
  input  B,
  input  C,
  output S
);

  wire and_1_out, or_1_out, xor_1_out;

  xor xor_1 (xor_1_out, A, B);
  or or_1 (or_1_out, xor_1_out, ~B);  // OR_Gate
  and and_1 (and_1_out, ~A, or_1_out);  // AND_Gate
  or or_2 (S, and_1_out, ~C);  // OR_Gate
endmodule

module SUB_1 (
  input  in_1,
  input  in_2,
  input  in_3,
  output out_4,
  output out_5
);

  wire and_1_out, and_2_out, or_1_out, xor_1_out;

  xor xor_1 (xor_1_out, in_2, in_1);
  or or_1 (or_1_out, in_3, in_2);
  and and_1 (and_1_out, in_3, in_2);
  xor xor_2 (out_4, in_3, xor_1_out);
  and and_2 (and_2_out, or_1_out, ~in_1);  // AND_Gate
  or or_2 (out_5, and_2_out, and_1_out);
endmodule
